# Fritzing sketch P2-LEITURA_BOTAO_ESQUEMA (saved by Fritzing 0.9.3b)
breadboards: 1

parts:
  U1 = ESP32-38PinWide [part_number=ESP32-38PinWide]
  R1 = Resistor [tolerance=±5% resistance=330 package=THT]
  LED1 = LED - 5mm [color="Red (633nm)" package="5 mm [THT]"]
  S1 = Momentary Switch [package=ksa_sealed_tac_switch]
  R2 = Resistor [tolerance=±5% resistance=10k package=THT]

nets:
  N1: U1.3.3, S1.1
  N2: U1.GPIO35, S1.4, R2.Pin_0
  N3: U1.GPIO27, R1.Pin_1
  N4: U1.GND, LED1.cathode, R2.Pin_1
  N5: R1.Pin_0, LED1.anode

custom parts:
  ESP32-38PinWide: Generic 38-Pin ESP32 with wide format (only access to one side of pins on a breadboard) based on Stephen Lilley's HiLetgo ESP-WROOM-32 ESP32 ESP-32S Development Board.
